# Fritzing sketch Coeur LED (saved by Fritzing 0.9.3b)
breadboards: 2

parts:
  Composant1 = Arduino Uno (Rev3) - ICSP
  LED1 = LED - 5mm [color="Red (633nm)" package="5 mm [THT]"]
  LED2 = LED - 5mm [color="Red (633nm)" package="5 mm [THT]"]
  LED3 = LED - 5mm [color="Red (633nm)" package="5 mm [THT]"]
  LED4 = LED - 5mm [color="Red (633nm)" package="5 mm [THT]"]
  LED5 = LED - 5mm [color="Red (633nm)" package="5 mm [THT]"]
  LED6 = LED - 5mm [color="Red (633nm)" package="5 mm [THT]"]
  LED7 = LED - 5mm [color="Red (633nm)" package="5 mm [THT]"]
  LED8 = LED - 5mm [color="Red (633nm)" package="5 mm [THT]"]
  LED9 = LED - 5mm [color="Red (633nm)" package="5 mm [THT]"]
  LED10 = LED - 5mm [color="Red (633nm)" package="5 mm [THT]"]
  R4 = Resistor [tolerance=±5% resistance=220 package="0603 [SMD]"]
  R5 = Resistor [tolerance=±5% resistance=220 package="0603 [SMD]"]
  R6 = Resistor [tolerance=±5% resistance=220 package="0603 [SMD]"]
  R8 = Resistor [tolerance=±5% resistance=220 package="0603 [SMD]"]
  R9 = Resistor [tolerance=±5% resistance=220 package="0603 [SMD]"]
  R10 = Resistor [tolerance=±5% resistance=220 package="0603 [SMD]"]
  R11 = Resistor [tolerance=±5% resistance=220 package="0603 [SMD]"]
  R12 = Resistor [tolerance=±5% resistance=220 package="0603 [SMD]"]
  R13 = Resistor [tolerance=±5% resistance=220 package="0603 [SMD]"]
  R14 = Resistor [tolerance=±5% resistance=220 package="0603 [SMD]"]

nets:
  N1: Composant1.ICSP_MOSI, Composant1.D9_PWM, Composant1.D11_PWM/MOSI, Composant1.GND, Composant1.D3_PWM, LED1.cathode, LED2.cathode, LED3.cathode, LED4.cathode, LED5.cathode, LED6.anode, LED7.cathode, LED8.cathode, LED9.cathode, LED10.cathode, R14.Pin_1
  N2: Composant1.D8, R5.Pin_1
  N3: Composant1.D12/MISO, R14.Pin_0
  N4: Composant1.D5_PWM, R8.Pin_1
  N5: Composant1.D6_PWM, R10.Pin_1
  N6: Composant1.D7, R6.Pin_1
  N7: LED1.anode, R4.Pin_1
  N8: LED2.anode, R11.Pin_1
  N9: LED3.anode, R6.Pin_0
  N10: LED4.anode, R8.Pin_0
  N11: LED7.anode, R10.Pin_0
  N12: LED8.anode, R9.Pin_1
  N13: LED9.anode, R13.Pin_1
  N14: LED10.anode, R12.Pin_1
