# Fritzing sketch Module 1 (saved by Fritzing 0.9.3b)
breadboards: 1

parts:
  Composant1 = Arduino Uno (Rev3) - ICSP
  R1 = Resistor [tolerance=±5% resistance=22k package=THT]
  C1 = Ceramic Capacitor [capacitance=1µF package="100 mil [THT, multilayer]"]
  LED1 = LED - 5mm [color="Infrared (940nm)" package="5 mm [THT]"]
  R2 = Resistor [tolerance=±5% resistance=2.2k package=THT]
  R3 = Photocell (LDR) [package=THT]
  R4 = Resistor [tolerance=±5% resistance=68k package=THT]
  R5 = Resistor [tolerance=±5% resistance=1k package=THT]
  U1 = LM124-324 Quad Opamp [package="DIP (Dual Inline)"]
  C2 = Ceramic Capacitor [capacitance=100nF package="100 mil [THT, multilayer]"]
  R6 = Resistor [tolerance=±5% resistance=100 package=THT]
  R7 = Resistor [tolerance=±5% resistance=470k package=THT]
  LED2 = LED - 5mm [color="Red (633nm)" package="5 mm [THT]"]

nets:
  N1: Composant1.A0, R6.Pin_0, LED2.anode
  N2: Composant1.5V, R1.Pin_0, R2.Pin_0, U1.VCC+
  N3: Composant1.GND, LED1.cathode, R3.pin_0, R4.Pin_1, R5.Pin_1, U1.VCC-, LED2.cathode
  N4: R1.Pin_1, C1.0, R3.pin_1
  N5: C1.1, R4.Pin_0, U1.2IN+
  N6: LED1.anode, R2.Pin_1
  N7: U1.2IN-, C2.1, R7.Pin_0
  N8: U1.2OUT, C2.0, R6.Pin_1, R7.Pin_1
